# Fritzing sketch RaspberryCar (saved by Fritzing 0.9.3b)

parts:
  S1 = H-Bridge with L298N
  Raspberry_Pi_2 = Raspberry Pi 3 [part_number=RPI-3-V1.2]
  M4 = DC Motor
  M3 = DC Motor
  VCC1 = Battery block 9V

nets:
  N1: S1.12V, VCC1.+
  GND: S1.GND, Raspberry_Pi_2.GND, VCC1.-
  N2: S1.ENA, Raspberry_Pi_2.GPIO23
  N3: S1.IN1, Raspberry_Pi_2.GPIO17
  N4: S1.IN2, Raspberry_Pi_2.GPIO18
  N5: S1.IN3, Raspberry_Pi_2.GPIO27
  N6: S1.IN4, Raspberry_Pi_2.GPIO22
  N7: S1.ENB, Raspberry_Pi_2.GPIO24
  N8: S1.M1-01, M3.pin_2
  N9: S1.M1-02, M3.pin_1
  N10: S1.M2-01, M4.pin_1
  N11: S1.M2-02, M4.pin_2

custom parts:
  H-Bridge with L298N: h-bridge
